// Logisim project cpu.circ as structural Verilog: 8 circuits, main circuit Alu
module main (
  input  in_1,
  output out_2
);

  wire alu_2_zero, and_1_out, and_2_out, clock_1_out, control_1_alusrc1, control_1_branch,
       control_1_mem_read, control_1_mr, control_1_mw, control_1_regdst, control_1_rw, control_1_stp000111,
       not_1_out, not_3_out;
  wire [1:0] control_1_aluop0;
  wire [3:0] alu_2_result, alu_2_result_2, alu_2_result_3, alu_2_result_4, alu_2_result_5, alu_2_result_6,
       alu_2_result_7, alu_2_result_8, alucontrol_1_out_op, datamemor_1_rd_2, instruction_reg_1_out_2,
       instruction_reg_1_out_2_2, instruction_reg_1_out_2_3, instruction_reg_1_out_2_4,
       instruction_reg_1_out_2_5, instruction_reg_1_out_2_6, instruction_reg_1_out_2_7,
       instruction_reg_1_out_2_8;
  wire [4:0] multiplexer_1_out;
  wire [27:0] datamemor_1_rd;
  wire [31:0] alu_1_result, alu_3_result, bit_extender_1_out, multiplexer_2_out, multiplexer_3_out,
       multiplexer_4_out, pc_1_out_4, regdui_1_readdata1, regdui_1_readdata2, shifter_1_out;

  pc pc_1 (.cin(multiplexer_3_out), .reset(in_1), .clk(and_1_out), .out_4(pc_1_out_4));
  not not_1 (not_1_out, control_1_stp000111);
  not not_2 (out_2, control_1_stp000111);
  and and_1 (and_1_out, not_1_out, clock_1_out);
  instruction_reg instruction_reg_1 (
    .in_1(pc_1_out_4),
    .out_2({instruction_reg_1_out_2_8, instruction_reg_1_out_2_7, instruction_reg_1_out_2_6, instruction_reg_1_out_2_5, instruction_reg_1_out_2_4, instruction_reg_1_out_2_3, instruction_reg_1_out_2_2, instruction_reg_1_out_2}));
  Multiplexer #(.width(5)) multiplexer_1 (
    .in0({instruction_reg_1_out_2_6[0], instruction_reg_1_out_2_5}),
    .in1({instruction_reg_1_out_2_4, instruction_reg_1_out_2_3[3]}), .out(multiplexer_1_out),
    .sel(control_1_regdst));
  assign bit_extender_1_out = {{16{instruction_reg_1_out_2_4[3]}}, {instruction_reg_1_out_2_4, instruction_reg_1_out_2_3, instruction_reg_1_out_2_2, instruction_reg_1_out_2}};  // Bit_Extender bit_extender_1
  control control_1 (
    .Opcode({instruction_reg_1_out_2_8, instruction_reg_1_out_2_7[3:2]}), .regdst(control_1_regdst),
    .branch(control_1_branch), .mem_read(control_1_mem_read), .mr(control_1_mr), .aluop0(control_1_aluop0),
    .mw(control_1_mw), .alusrc1(control_1_alusrc1), .rw(control_1_rw), .stp000111(control_1_stp000111));
  regDui regdui_1 (
    .ReadReg1({instruction_reg_1_out_2_7[1:0], instruction_reg_1_out_2_6[3:1]}),
    .ReadReg2({instruction_reg_1_out_2_6[0], instruction_reg_1_out_2_5}), .RegWrite(control_1_rw),
    .WriteReg(multiplexer_1_out), .WriteData(multiplexer_4_out), .CLK(and_1_out),
    .ReadData1(regdui_1_readdata1), .ReadData2(regdui_1_readdata2));
  Multiplexer #(.width(32)) multiplexer_2 (
    .in0(regdui_1_readdata2), .in1(bit_extender_1_out), .out(multiplexer_2_out), .sel(control_1_alusrc1));
  Alu alu_1 (.ALUControl(4'b0010), .a(pc_1_out_4), .b(32'h4), .result(alu_1_result));  // open: zero
  Shifter #(.width(32)) shifter_1 (.in(bit_extender_1_out), .\dist (5'b00010), .out(shifter_1_out));
  Hex_Digit_Display hex_digit_display_1 (.value(instruction_reg_1_out_2_8));  // open: dp
  Hex_Digit_Display hex_digit_display_2 (.value(instruction_reg_1_out_2_7));  // open: dp
  Hex_Digit_Display hex_digit_display_3 (.value(alu_2_result_8));  // open: dp
  aluControl alucontrol_1 (.aluop(control_1_aluop0), .f(instruction_reg_1_out_2), .out_op(alucontrol_1_out_op));
  Hex_Digit_Display hex_digit_display_4 (.value(instruction_reg_1_out_2_6));  // open: dp
  Hex_Digit_Display hex_digit_display_5 (.value(instruction_reg_1_out_2_5));  // open: dp
  Alu alu_2 (
    .ALUControl(alucontrol_1_out_op), .a(regdui_1_readdata1), .b(multiplexer_2_out), .zero(alu_2_zero),
    .result({alu_2_result_8, alu_2_result_7, alu_2_result_6, alu_2_result_5, alu_2_result_4, alu_2_result_3, alu_2_result_2, alu_2_result}));
  Hex_Digit_Display hex_digit_display_6 (.value(alu_2_result_7));  // open: dp
  Hex_Digit_Display hex_digit_display_7 (.value(alu_2_result_6));  // open: dp
  Hex_Digit_Display hex_digit_display_8 (.value(instruction_reg_1_out_2_4));  // open: dp
  Hex_Digit_Display hex_digit_display_9 (.value(instruction_reg_1_out_2_3));  // open: dp
  not not_3 (not_3_out, alu_2_zero);
  Hex_Digit_Display hex_digit_display_10 (.value(alu_2_result_5));  // open: dp
  Hex_Digit_Display hex_digit_display_11 (.value(alu_2_result_4));  // open: dp
  Hex_Digit_Display hex_digit_display_12 (.value(instruction_reg_1_out_2_2));  // open: dp
  Hex_Digit_Display hex_digit_display_13 (.value(instruction_reg_1_out_2));  // open: dp
  Alu alu_3 (.ALUControl(4'b0010), .a(alu_1_result), .b(shifter_1_out), .result(alu_3_result));  // open: zero
  and and_2 (and_2_out, control_1_branch, not_3_out);
  Hex_Digit_Display hex_digit_display_14 (.value(alu_2_result_3));  // open: dp
  Hex_Digit_Display hex_digit_display_15 (.value(alu_2_result_2));  // open: dp
  Hex_Digit_Display hex_digit_display_16 (.value(alu_2_result));  // open: dp
  Multiplexer #(.width(32)) multiplexer_3 (
    .in0(alu_1_result), .in1(alu_3_result), .out(multiplexer_3_out), .sel(and_2_out));
  Hex_Digit_Display hex_digit_display_17 (.value(datamemor_1_rd_2));  // open: dp
  DataMemor datamemor_1 (
    .ra1({alu_2_result_8, alu_2_result_7, alu_2_result_6, alu_2_result_5, alu_2_result_4, alu_2_result_3, alu_2_result_2, alu_2_result}),
    .wd(regdui_1_readdata2), .mw(control_1_mw), .mr(control_1_mem_read), .clk1(and_1_out),
    .rd({datamemor_1_rd_2, datamemor_1_rd}));
  Hex_Digit_Display hex_digit_display_18 (.value(datamemor_1_rd[27:24]));  // open: dp
  Hex_Digit_Display hex_digit_display_19 (.value(datamemor_1_rd[23:20]));  // open: dp
  Hex_Digit_Display hex_digit_display_20 (.value(datamemor_1_rd[19:16]));  // open: dp
  Hex_Digit_Display hex_digit_display_21 (.value(datamemor_1_rd[15:12]));  // open: dp
  Hex_Digit_Display hex_digit_display_22 (.value(datamemor_1_rd[11:8]));  // open: dp
  Hex_Digit_Display hex_digit_display_23 (.value(datamemor_1_rd[7:4]));  // open: dp
  Clock clock_1 (.out(clock_1_out));
  Multiplexer #(.width(32)) multiplexer_4 (
    .in0({alu_2_result_8, alu_2_result_7, alu_2_result_6, alu_2_result_5, alu_2_result_4, alu_2_result_3, alu_2_result_2, alu_2_result}),
    .in1({datamemor_1_rd_2, datamemor_1_rd}), .out(multiplexer_4_out), .sel(control_1_mr));
  Hex_Digit_Display hex_digit_display_24 (.value(datamemor_1_rd[3:0]));  // open: dp
endmodule

module Alu (
  input  [3:0] ALUControl,
  input  [31:0] a,
  input  [31:0] b,
  output zero,
  output [31:0] result
);

  wire [31:0] adder_1_out, and_1_out, or_1_out, subtractor_1_out;

  assign and_1_out = a & b;  // AND_Gate and_1, 32 bits wide
  assign or_1_out = a | b;  // OR_Gate or_1, 32 bits wide
  Adder #(.width(32)) adder_1 (.a(a), .b(b), .out(adder_1_out));  // open: cin, cout
  Subtractor #(.width(32)) subtractor_1 (.a(a), .b(b), .out(subtractor_1_out));  // open: bin, bout
  Multiplexer #(.select(4), .width(32)) multiplexer_1 (
    .in0(and_1_out), .in1(or_1_out), .in2(adder_1_out), .in6(subtractor_1_out), .out(result), .sel(ALUControl));  // open: in3, in4, in5, in7, in8, in9, in10, in11, in12, in13, in14, in15
  and and_2 (zero, ~result[0], ~result[1], ~result[2], ~result[3], ~result[4], ~result[5], ~result[6], ~result[7], ~result[8], ~result[9], ~result[10], ~result[11], ~result[12], ~result[13], ~result[14], ~result[15], ~result[16], ~result[17], ~result[18], ~result[19], ~result[20], ~result[21], ~result[22], ~result[23], ~result[24], ~result[25], ~result[26], ~result[27], ~result[28], ~result[29], ~result[30], ~result[31]);  // AND_Gate
endmodule

module aluControl (
  input  [1:0] aluop,
  input  [3:0] f,
  output [3:0] out_op
);

  wire and_1_out, and_2_out, and_3_out, not_1_out, not_2_out;

  not not_1 (not_1_out, aluop[1]);
  not not_2 (not_2_out, f[2]);
  not not_3 (out_op[3], 1'b1);
  and and_1 (and_1_out, aluop[1], f[1]);
  or or_1 (out_op[1], not_1_out, not_2_out);
  and and_2 (and_2_out, aluop[1], f[0]);
  and and_3 (and_3_out, aluop[1], f[3]);
  or or_2 (out_op[2], aluop[0], and_1_out);
  or or_3 (out_op[0], and_2_out, and_3_out);
endmodule

module pc (
  input  [31:0] cin,
  input  reset,
  input  clk,
  output [31:0] out_4
);

  Register #(.trigger("falling"), .width(32)) register_1 (.D(cin), .clk(clk), .Q(out_4), .clr(reset));  // open: en
endmodule

module regDui (
  input  [4:0] ReadReg1,
  input  [4:0] ReadReg2,
  input  RegWrite,
  input  [4:0] WriteReg,
  input  [31:0] WriteData,
  input  CLK,
  output [31:0] ReadData1,
  output [31:0] ReadData2
);

  wire demultiplexer_1_out0, demultiplexer_1_out1, demultiplexer_1_out2, demultiplexer_1_out3,
       demultiplexer_1_out4, demultiplexer_1_out5, demultiplexer_1_out6, demultiplexer_1_out7,
       demultiplexer_1_out8, demultiplexer_1_out9, demultiplexer_1_out10, demultiplexer_1_out11,
       demultiplexer_1_out12, demultiplexer_1_out13, demultiplexer_1_out14, demultiplexer_1_out15,
       demultiplexer_1_out16, demultiplexer_1_out17, demultiplexer_1_out18, demultiplexer_1_out19,
       demultiplexer_1_out20, demultiplexer_1_out21, demultiplexer_1_out22, demultiplexer_1_out23,
       demultiplexer_1_out24, demultiplexer_1_out25, demultiplexer_1_out26, demultiplexer_1_out27,
       demultiplexer_1_out28, demultiplexer_1_out29, demultiplexer_1_out30, demultiplexer_1_out31;
  wire [31:0] a0_q, a1_q, a2_q, a3_q, at_q, fp_q, gp_q, k0_q, k1_q, ra_q, s0_q, s1_q, s2_q, s3_q, s4_q, s5_q,
       s6_q, s7_q, sp_q, t0_q, t1_q, t2_q, t3_q, t4_q, t5_q, t6_q, t7_q, t8_q, t9_q, v0_q, v1_q, zero_q;

  Demultiplexer #(.select(5)) demultiplexer_1 (
    .out0(demultiplexer_1_out0), .out1(demultiplexer_1_out1), .out2(demultiplexer_1_out2),
    .out3(demultiplexer_1_out3), .out4(demultiplexer_1_out4), .out5(demultiplexer_1_out5),
    .out6(demultiplexer_1_out6), .out7(demultiplexer_1_out7), .out8(demultiplexer_1_out8),
    .out9(demultiplexer_1_out9), .out10(demultiplexer_1_out10), .out11(demultiplexer_1_out11),
    .out12(demultiplexer_1_out12), .out13(demultiplexer_1_out13), .out14(demultiplexer_1_out14),
    .out15(demultiplexer_1_out15), .out16(demultiplexer_1_out16), .out17(demultiplexer_1_out17),
    .out18(demultiplexer_1_out18), .out19(demultiplexer_1_out19), .out20(demultiplexer_1_out20),
    .out21(demultiplexer_1_out21), .out22(demultiplexer_1_out22), .out23(demultiplexer_1_out23),
    .out24(demultiplexer_1_out24), .out25(demultiplexer_1_out25), .out26(demultiplexer_1_out26),
    .out27(demultiplexer_1_out27), .out28(demultiplexer_1_out28), .out29(demultiplexer_1_out29),
    .out30(demultiplexer_1_out30), .out31(demultiplexer_1_out31), .in(RegWrite), .sel(WriteReg));
  Register #(.width(32)) zero (.D(WriteData), .en(demultiplexer_1_out0), .clk(CLK), .Q(zero_q));  // open: clr
  Register #(.trigger("falling"), .width(32)) a0 (
    .D(WriteData), .en(demultiplexer_1_out4), .clk(CLK), .Q(a0_q));  // open: clr
  Register #(.trigger("falling"), .width(32)) t0 (
    .D(WriteData), .en(demultiplexer_1_out8), .clk(CLK), .Q(t0_q));  // open: clr
  Register #(.trigger("falling"), .width(32)) t4 (
    .D(WriteData), .en(demultiplexer_1_out12), .clk(CLK), .Q(t4_q));  // open: clr
  Register #(.trigger("falling"), .width(32)) s0 (
    .D(WriteData), .en(demultiplexer_1_out16), .clk(CLK), .Q(s0_q));  // open: clr
  Register #(.trigger("falling"), .width(32)) s4 (
    .D(WriteData), .en(demultiplexer_1_out20), .clk(CLK), .Q(s4_q));  // open: clr
  Register #(.trigger("falling"), .width(32)) t8 (
    .D(WriteData), .en(demultiplexer_1_out24), .clk(CLK), .Q(t8_q));  // open: clr
  Register #(.trigger("falling"), .width(32)) gp (
    .D(WriteData), .en(demultiplexer_1_out28), .clk(CLK), .Q(gp_q));  // open: clr
  Register #(.width(32)) at (.D(WriteData), .en(demultiplexer_1_out1), .clk(CLK), .Q(at_q));  // open: clr
  Register #(.trigger("falling"), .width(32)) a1 (
    .D(WriteData), .en(demultiplexer_1_out5), .clk(CLK), .Q(a1_q));  // open: clr
  Register #(.trigger("falling"), .width(32)) t1 (
    .D(WriteData), .en(demultiplexer_1_out9), .clk(CLK), .Q(t1_q));  // open: clr
  Register #(.trigger("falling"), .width(32)) t5 (
    .D(WriteData), .en(demultiplexer_1_out13), .clk(CLK), .Q(t5_q));  // open: clr
  Register #(.trigger("falling"), .width(32)) s1 (
    .D(WriteData), .en(demultiplexer_1_out17), .clk(CLK), .Q(s1_q));  // open: clr
  Register #(.trigger("falling"), .width(32)) s5 (
    .D(WriteData), .en(demultiplexer_1_out21), .clk(CLK), .Q(s5_q));  // open: clr
  Register #(.trigger("falling"), .width(32)) t9 (
    .D(WriteData), .en(demultiplexer_1_out25), .clk(CLK), .Q(t9_q));  // open: clr
  Register #(.trigger("falling"), .width(32)) sp (
    .D(WriteData), .en(demultiplexer_1_out29), .clk(CLK), .Q(sp_q));  // open: clr
  Register #(.width(32)) v0 (.D(WriteData), .en(demultiplexer_1_out2), .clk(CLK), .Q(v0_q));  // open: clr
  Register #(.trigger("falling"), .width(32)) a2 (
    .D(WriteData), .en(demultiplexer_1_out6), .clk(CLK), .Q(a2_q));  // open: clr
  Register #(.trigger("falling"), .width(32)) t2 (
    .D(WriteData), .en(demultiplexer_1_out10), .clk(CLK), .Q(t2_q));  // open: clr
  Register #(.trigger("falling"), .width(32)) t6 (
    .D(WriteData), .en(demultiplexer_1_out14), .clk(CLK), .Q(t6_q));  // open: clr
  Register #(.trigger("falling"), .width(32)) s2 (
    .D(WriteData), .en(demultiplexer_1_out18), .clk(CLK), .Q(s2_q));  // open: clr
  Register #(.trigger("falling"), .width(32)) s6 (
    .D(WriteData), .en(demultiplexer_1_out22), .clk(CLK), .Q(s6_q));  // open: clr
  Register #(.trigger("falling"), .width(32)) k0 (
    .D(WriteData), .en(demultiplexer_1_out26), .clk(CLK), .Q(k0_q));  // open: clr
  Register #(.trigger("falling"), .width(32)) fp (
    .D(WriteData), .en(demultiplexer_1_out30), .clk(CLK), .Q(fp_q));  // open: clr
  Register #(.width(32)) v1 (.D(WriteData), .en(demultiplexer_1_out3), .clk(CLK), .Q(v1_q));  // open: clr
  Register #(.trigger("falling"), .width(32)) a3 (
    .D(WriteData), .en(demultiplexer_1_out7), .clk(CLK), .Q(a3_q));  // open: clr
  Register #(.trigger("falling"), .width(32)) t3 (
    .D(WriteData), .en(demultiplexer_1_out11), .clk(CLK), .Q(t3_q));  // open: clr
  Register #(.trigger("falling"), .width(32)) t7 (
    .D(WriteData), .en(demultiplexer_1_out15), .clk(CLK), .Q(t7_q));  // open: clr
  Register #(.trigger("falling"), .width(32)) s3 (
    .D(WriteData), .en(demultiplexer_1_out19), .clk(CLK), .Q(s3_q));  // open: clr
  Register #(.trigger("falling"), .width(32)) s7 (
    .D(WriteData), .en(demultiplexer_1_out23), .clk(CLK), .Q(s7_q));  // open: clr
  Register #(.trigger("falling"), .width(32)) k1 (
    .D(WriteData), .en(demultiplexer_1_out27), .clk(CLK), .Q(k1_q));  // open: clr
  Register #(.trigger("falling"), .width(32)) ra (
    .D(WriteData), .en(demultiplexer_1_out31), .clk(CLK), .Q(ra_q));  // open: clr
  Multiplexer #(.select(5), .width(32)) multiplexer_1 (
    .in0(zero_q), .in1(at_q), .in2(v0_q), .in3(v1_q), .in4(a0_q), .in5(a1_q), .in6(a2_q), .in7(a3_q),
    .in8(t0_q), .in9(t1_q), .in10(t2_q), .in11(t3_q), .in12(t4_q), .in13(t5_q), .in14(t6_q), .in15(t7_q),
    .in16(s0_q), .in17(s1_q), .in18(s2_q), .in19(s3_q), .in20(s4_q), .in21(s5_q), .in22(s6_q), .in23(s7_q),
    .in24(t8_q), .in25(t9_q), .in26(k0_q), .in27(k1_q), .in28(gp_q), .in29(sp_q), .in30(fp_q), .in31(ra_q),
    .out(ReadData1), .sel(ReadReg1));
  Multiplexer #(.select(5), .width(32)) multiplexer_2 (
    .in0(zero_q), .in1(at_q), .in2(v0_q), .in3(v1_q), .in4(a0_q), .in5(a1_q), .in6(a2_q), .in7(a3_q),
    .in8(t0_q), .in9(t1_q), .in10(t2_q), .in11(t3_q), .in12(t4_q), .in13(t5_q), .in14(t6_q), .in15(t7_q),
    .in16(s0_q), .in17(s1_q), .in18(s2_q), .in19(s3_q), .in20(s4_q), .in21(s5_q), .in22(s6_q), .in23(s7_q),
    .in24(t8_q), .in25(t9_q), .in26(k0_q), .in27(k1_q), .in28(gp_q), .in29(sp_q), .in30(fp_q), .in31(ra_q),
    .out(ReadData2), .sel(ReadReg2));
endmodule

module control (
  input  [5:0] Opcode,
  output regdst,
  output branch,
  output mem_read,
  output mr,
  output [1:0] aluop0,
  output mw,
  output alusrc1,
  output rw,
  output stp000111
);

  and Tipo_R (aluop0[1], ~Opcode[5], ~Opcode[4], ~Opcode[3], ~Opcode[2], ~Opcode[1], ~Opcode[0]);  // AND_Gate
  and lw (mem_read, Opcode[5], ~Opcode[4], ~Opcode[3], ~Opcode[2], Opcode[1], Opcode[0]);  // AND_Gate
  and sw (mw, Opcode[5], ~Opcode[4], Opcode[3], ~Opcode[2], Opcode[1], Opcode[0]);  // AND_Gate
  and bne (aluop0[0], ~Opcode[5], ~Opcode[4], ~Opcode[3], Opcode[2], ~Opcode[1], Opcode[0]);  // AND_Gate
  or or_1 (alusrc1, mw, mem_read);
  or or_2 (rw, mem_read, aluop0[1]);
  and and_1 (stp000111, Opcode[5], Opcode[4], Opcode[3], Opcode[0], Opcode[2], Opcode[1]);

  assign branch = aluop0[0];
  assign mr = mem_read;
  assign regdst = aluop0[1];
endmodule

module DataMemor (
  input  [31:0] ra1,
  input  [31:0] wd,
  input  mw,
  input  mr,
  input  clk1,
  output [31:0] rd
);

  RAM #(.addrWidth(24), .dataWidth(32)) ram_1 (.addr(ra1[23:0]), .we(mw), .oe(mr), .clk(clk1), .din(wd), .dout(rd));
endmodule

module instruction_reg (
  input  [31:0] in_1,
  output [31:0] out_2
);

  ROM #(.addrWidth(24), .dataWidth(32)) rom_1 (.addr(in_1[25:2]), .data(out_2));

  // Notes on the sheet:
  //   contents of rom_1 (hex, n*v repeats v):
  //   8c100000 8c110008 8c120004 8c13000c 8c140010 8c150004 2b14020 100a820 2114022 1008020 1650fffb
  //   2754025 2884824 ac090014 8c100014 fc000000
endmodule
